// Digital circuit 32位计算机.dig as structural Verilog
module \_32位计算机  (
  input  Clock,
  output [7:0] out_2,
  output [3:0] out_3,
  output [31:0] out_4
);

  wire add_1_c_o, and_3_out, and_4_out, and_5_out, and_6_out, and_7_out, clock_t, comparator_1_eq,
       comparator_2_eq, CS_RAM, CS_ROM, CS_SP, END_CYCLE, Flag_c, Flag_z, HALT, INC_PC, JC_eq, JNC_eq,
       JNZ_eq, JZ_eq, LD_IR, LD_MAR, LD_MDREXT, LD_MDRINT, LD_PC, LD_RFlags, LD_Rw, multiplexer_2_out,
       not_1_out, not_3_out, not_4_out, OE, OE_ALU, OE_MDREXT, OE_MDRINT, OE_PC, OE_Ra, OE_Rb, or_2_out,
       sub_1_c_o, WE;
  wire [3:0] ADDR_Ra, ADDR_Rb, ADDR_Rw, MODE_ALU;
  wire [20:0] CU_d;
  wire [31:0] add_1_s, and_2_out, barrelshifter_1_out, DEC_s, div_1_q, div_1_r, driver_1_out, driver_6_out,
       INC_s, MAR_q, MDR_EXT_q, MDR_INT_q, multiplexer_1_out, nand_1_out, nor_1_out, not_2_out, or_1_out,
       RegFile_da, RegFile_db, sub_1_s, xnor_1_out, xor_1_out;
  wire [31:20] IR_q;
  wire [63:0] mul_1_mul;

  CounterPreset #(.Bits(32), .isProgramCounter("true")) PC (
    .en(INC_PC), .C(clock_t), .dir(1'b0), .in(driver_1_out), .ld(LD_PC), .clr(1'b0), .out(out_4));  // open: ovf
  not not_1 (not_1_out, HALT);
  and and_1 (clock_t, Clock, not_1_out);
  assign driver_1_out = OE_PC ? out_4 : 32'bz;  // Driver driver_1
  CounterPreset #(.maxValue(15), .Bits(4)) STATE (
    .en(1'b1), .C(clock_t), .dir(1'b0), .in(4'b0000), .ld(1'b0), .clr(END_CYCLE), .out(out_3));  // open: ovf
  Register #(.Bits(32)) IR (.D(driver_1_out), .C(clock_t), .en(LD_IR), .Q({IR_q, ADDR_Ra, ADDR_Rb, ADDR_Rw, out_2}));
  assign driver_1_out = OE_Ra ? RegFile_da : 32'bz;  // Driver driver_2
  RegisterFile #(.AddrBits(4), .Bits(32)) RegFile (
    .Din(driver_1_out), .we(LD_Rw), .Rw(ADDR_Rw), .C(clock_t), .Ra(ADDR_Ra), .Rb(ADDR_Rb), .Da(RegFile_da),
    .Db(RegFile_db));
  assign driver_1_out = OE_Rb ? RegFile_db : 32'bz;  // Driver driver_3
  ROM #(.AddrBits(12), .isProgramMemory("true"), .Bits(22)) CU (
    .A({out_2, out_3}), .sel(1'b1),
    .D({END_CYCLE, CU_d[20], MODE_ALU, WE, OE, INC_PC, OE_ALU, OE_Rb, OE_Ra, OE_MDREXT, OE_MDRINT, OE_PC, LD_RFlags, LD_Rw, LD_IR, LD_MDREXT, LD_MDRINT, LD_MAR, CU_d[0]}));
  assign driver_1_out = OE_ALU ? multiplexer_1_out : 32'bz;  // Driver driver_4
  Add #(.Bits(32)) add_1 (.a(RegFile_da), .b(RegFile_db), .c_i(1'b0), .s(add_1_s), .c_o(add_1_c_o));
  Sub #(.Bits(32)) sub_1 (.a(RegFile_da), .b(RegFile_db), .c_i(1'b0), .s(sub_1_s), .c_o(sub_1_c_o));
  Mul #(.Bits(32)) mul_1 (.a(RegFile_da), .b(RegFile_db), .mul(mul_1_mul));
  Div #(.Bits(32)) div_1 (.a(RegFile_da), .b(RegFile_db), .q(div_1_q), .r(div_1_r));
  BarrelShifter #(.Bits(32)) barrelshifter_1 (.in(RegFile_da), .shift(RegFile_db[5:0]), .out(barrelshifter_1_out));
  assign and_2_out = RegFile_da & RegFile_db;  // And and_2, 32 bits wide
  assign nand_1_out = ~(RegFile_da & RegFile_db);  // NAnd nand_1, 32 bits wide
  assign or_1_out = RegFile_da | RegFile_db;  // Or or_1, 32 bits wide
  assign nor_1_out = ~(RegFile_da | RegFile_db);  // NOr nor_1, 32 bits wide
  assign xor_1_out = RegFile_da ^ RegFile_db;  // XOr xor_1, 32 bits wide
  assign xnor_1_out = ~(RegFile_da ^ RegFile_db);  // XNOr xnor_1, 32 bits wide
  assign not_2_out = ~RegFile_da;  // Not not_2, 32 bits wide
  Add #(.Bits(32)) INC (.a(RegFile_da), .b(32'h1), .c_i(1'b0), .s(INC_s));  // open: c_o
  Sub #(.Bits(32)) DEC (.a(RegFile_da), .b(32'h1), .c_i(1'b0), .s(DEC_s));  // open: c_o
  Comparator #(.Bits(8)) JC (.a(out_2), .b(8'h32), .eq(JC_eq));  // open: gt, lt
  Comparator #(.Bits(8)) JZ (.a(out_2), .b(8'h33), .eq(JZ_eq));  // open: gt, lt
  Comparator #(.Bits(8)) JNC (.a(out_2), .b(8'h34), .eq(JNC_eq));  // open: gt, lt
  Comparator #(.Bits(8)) JNZ (.a(out_2), .b(8'h35), .eq(JNZ_eq));  // open: gt, lt
  not not_3 (not_3_out, Flag_c);
  not not_4 (not_4_out, Flag_z);
  and and_3 (and_3_out, JC_eq, Flag_c);
  and and_4 (and_4_out, JZ_eq, Flag_z);
  and and_5 (and_5_out, JNC_eq, not_3_out);
  and and_6 (and_6_out, JNZ_eq, not_4_out);
  and and_7 (and_7_out, CU_d[20], or_2_out);
  or or_2 (or_2_out, and_3_out, and_4_out, and_5_out, and_6_out);
  or or_3 (LD_PC, and_7_out, CU_d[0]);
  assign driver_1_out = OE_MDRINT ? MDR_INT_q : 32'bz;  // Driver driver_5
  Register #(.Bits(32)) MDR_EXT (.D(driver_1_out), .C(clock_t), .en(LD_MDREXT), .Q(MDR_EXT_q));
  Register #(.Bits(32)) MDR_INT (.D(driver_6_out), .C(clock_t), .en(LD_MDRINT), .Q(MDR_INT_q));
  assign driver_6_out = OE_MDREXT ? MDR_EXT_q : 32'bz;  // Driver driver_6
  Comparator #(.Bits(8)) u_HALT (.a(out_2), .b(8'hf0), .eq(HALT));  // open: gt, lt
  Multiplexer #(.Selector_Bits(4), .Bits(32)) multiplexer_1 (
    .sel(MODE_ALU), .in_0(add_1_s), .in_1(sub_1_s), .in_2(mul_1_mul[31:0]), .in_3(div_1_q),
    .in_4(barrelshifter_1_out), .in_5(and_2_out), .in_6(nand_1_out), .in_7(or_1_out), .in_8(nor_1_out),
    .in_9(xor_1_out), .in_10(xnor_1_out), .in_11(not_2_out), .in_12(INC_s), .in_13(DEC_s), .in_14(div_1_r),
    .in_15({32{1'b0}}), .out(multiplexer_1_out));
  Register #(.Bits(32)) MAR (.D(driver_1_out), .C(clock_t), .en(LD_MAR), .Q(MAR_q));
  Comparator #(.Bits(32)) comparator_1 (.a({32{1'b0}}), .b(multiplexer_1_out), .eq(comparator_1_eq));  // open: gt, lt
  Comparator #(.Bits(4)) comparator_2 (.a(MODE_ALU), .b(4'b0001), .eq(comparator_2_eq));  // open: gt, lt
  Multiplexer multiplexer_2 (.sel(comparator_2_eq), .in_0(add_1_c_o), .in_1(sub_1_c_o), .out(multiplexer_2_out));
  Register register_1 (.D(comparator_1_eq), .C(clock_t), .en(LD_RFlags), .Q(Flag_z));
  Register register_2 (.D(multiplexer_2_out), .C(clock_t), .en(LD_RFlags), .Q(Flag_c));
  Decoder #(.Selector_Bits(4)) decoder_1 (
    .sel(MAR_q[27:24]), .out_0(CS_ROM), .out_1(CS_RAM), .out_2(CS_SP));  // open: out_3, out_4, out_5, out_6, out_7, out_8, out_9, out_10, out_11, out_12, out_13, out_14, out_15
  EEPROM #(.AddrBits(24), .Bits(32)) ROM (.A(MAR_q[23:0]), .CS(CS_ROM), .WE(1'b0), .OE(OE), .D(driver_6_out));
  RAMSinglePortSel #(.AddrBits(24), .Bits(32)) RAM (.A(MAR_q[23:0]), .CS(CS_RAM), .WE(WE), .OE(OE), .D(driver_6_out));
  RAMSinglePortSel #(.AddrBits(24), .Bits(32)) SP (.A(MAR_q[23:0]), .CS(CS_SP), .WE(WE), .OE(OE), .D(driver_6_out));

  // Notes on the sheet:
  //   Clock: Hz: 6553600
  //   ALU
  //   contents of CU (hex, n*v repeats v):
  //   f0082,f6004,f0110,2f0000,12*0,f0082,f6004,f0110,2f0000,12*0,f0082
  //   ,f6004,f0110,2f0000,12*0,f0082,f6004,f0110,2f0000,12*0,f0082,f6004
  //   ,f0110,2f0000,12*0,f0082,f6004,f0110,2f0000,12*0,f0082,f6004,f0110
  //   ,2f0000,12*0,f0082,f6004,f0110,2f0000,12*0,f0082,f6004,f0110,2f0000
  //   ,12*0,f0082,f6004,f0110,2f0000,12*0,f0082,f6004,f0110,2f0000,12*0
  //   ,f0082,f6004,f0110,2f0000,12*0,f0082,f6004,f0110,2f0000,12*0,f0082
  //   ,f6004,f0110,2f0000,12*0,f0082,f6004,f0110,2f0000,12*0,f0082,f6004
  //   ,f0110,2f0000,12*0,f0082,f6004,f0110,2f0420,12*0,f0082,f6004,f0110
  //   ,f0802,f4004,2f0120,10*0,f0082,f6004,f0110,f0802,f0408,2f8200
  //   ,10*0,f0082,f6004,f0110,f0082,f6004,f0102,f4004,2f0120,8*0,f0082
  //   ,f6004,f0110,f0082,f6004,f0102,f0408,2f8200,8*0,f0082,f6004,f0110
  //   ,f2082,f4004,2f0120,10*0,f0082,f6004,f0110,f2082,f4004,2f0120
  //   ,10*0,f0082,f6004,f0110,1002,f4004,2f0120,10*0,f0082,f6004,f0110
  //   ,2f0000,12*0,f0082,f6004,f0110,2f0000,12*0,f0082,f6004,f0110,2f0000
  //   ,12*0,f0082,f6004,f0110,2f0000,12*0,f0082,f6004,f0110,2f0000,12*0
  //   ,f0082,f6004,f0110,2f0000,12*0,f0082,f6004,f0110,2f0000,12*0,f0082
  //   ,f6004,f0110,2f0000,12*0,f0082,f6004,f0110,201060,12*0,f0082,f6004
  //   ,f0110,211060,12*0,f0082,f6004,f0110,2c1020,12*0,f0082,f6004,f0110
  //   ,2d1020,12*0,f0082,f6004,f0110,221060,12*0,f0082,f6004,f0110,231060
  //   ,12*0,f0082,f6004,f0110,2e1060,12*0,f0082,f6004,f0110,241060,12*0
  //   ,f0082,f6004,f0110,251060,12*0,f0082,f6004,f0110,261060,12*0,f0082
  //   ,f6004,f0110,271060,12*0,f0082,f6004,f0110,281060,12*0,f0082,f6004
  //   ,f0110,291060,12*0,f0082,f6004,f0110,2a1060,12*0,f0082,f6004,f0110
  //   ,2b1060,12*0,f0082,f6004,f0110,211040,12*0,f0082,f6004,f0110,f0082
  //   ,f6004,2f0101,10*0,f0082,f6004,f0110,2f0401,12*0,f0082,f6004,f0110
  //   ,f0082,f6004,3f0100,10*0,f0082,f6004,f0110,f0082,f6004,3f0100
  //   ,10*0,f0082,f6004,f0110,f0082,f6004,3f0100,10*0,f0082,f6004,f0110
  //   ,f0082,f6004,3f0100,10*0,f0082,f6004,f0110,f2082,f4004,f0402,f0088
  //   ,f8200,c1020,3e0101,6*0,f0082,f6004,f0110,d1020,f0402,f4004,2f0101
  //   ,9*0,f0082,f6004,f0110,2f0000,12*0,f0082,f6004,f0110,2f0000,12*0
  //   ,f0082,f6004,f0110,2f0000,12*0,f0082,f6004,f0110,2f0000,12*0,f0082
  //   ,f6004,f0110,2f0000,12*0,f0082,f6004,f0110,2f0000,12*0,f0082,f6004
  //   ,f0110,2f0000,12*0,f0082,f6004,f0110,2f0000,12*0,f0082,f6004,f0110
  //   ,2f0000,12*0,f0082,f6004,f0110,2f0000,12*0,f0082,f6004,f0110,2f0000
  //   ,12*0,f0082,f6004,f0110,2f0000,12*0,f0082,f6004,f0110,2f0000,12*0
  //   ,f0082,f6004,f0110,2f0000,12*0,f0082,f6004,f0110,2f0000,12*0,f0082
  //   ,f6004,f0110,2f0000,12*0,f0082,f6004,f0110,2f0000,12*0,f0082,f6004
  //   ,f0110,2f0000,12*0,f0082,f6004,f0110,2f0000,12*0,f0082,f6004,f0110
  //   ,2f0000,12*0,f0082,f6004,f0110,2f0000,12*0,f0082,f6004,f0110,2f0000
  //   ,12*0,f0082,f6004,f0110,2f0000,12*0,f0082,f6004,f0110,2f0000,12*0
  //   ,f0082,f6004,f0110,2f0000,12*0,f0082,f6004,f0110,2f0000,12*0,f0082
  //   ,f6004,f0110,2f0000,12*0,f0082,f6004,f0110,2f0000,12*0,f0082,f6004
  //   ,f0110,2f0000,12*0,f0082,f6004,f0110,2f0000,12*0,f0082,f6004,f0110
  //   ,2f0000,12*0,f0082,f6004,f0110,2f0000,12*0,f0082,f6004,f0110,2f0000
  //   ,12*0,f0082,f6004,f0110,2f0000,12*0,f0082,f6004,f0110,2f0000,12*0
  //   ,f0082,f6004,f0110,2f0000,12*0,f0082,f6004,f0110,2f0000,12*0,f0082
  //   ,f6004,f0110,2f0000,12*0,f0082,f6004,f0110,2f0000,12*0,f0082,f6004
  //   ,f0110,2f0000,12*0,f0082,f6004,f0110,2f0000,12*0,f0082,f6004,f0110
  //   ,2f0000,12*0,f0082,f6004,f0110,2f0000,12*0,f0082,f6004,f0110,2f0000
  //   ,12*0,f0082,f6004,f0110,2f0000,12*0,f0082,f6004,f0110,2f0000,12*0
  //   ,f0082,f6004,f0110,2f0000,12*0,f0082,f6004,f0110,2f0000,12*0,f0082
  //   ,f6004,f0110,2f0000,12*0,f0082,f6004,f0110,2f0000,12*0,f0082,f6004
  //   ,f0110,2f0000,12*0,f0082,f6004,f0110,2f0000,12*0,f0082,f6004,f0110
  //   ,2f0000,12*0,f0082,f6004,f0110,2f0000,12*0,f0082,f6004,f0110,2f0000
  //   ,12*0,f0082,f6004,f0110,2f0000,12*0,f0082,f6004,f0110,2f0000,12*0
  //   ,f0082,f6004,f0110,2f0000,12*0,f0082,f6004,f0110,2f0000,12*0,f0082
  //   ,f6004,f0110,2f0000,12*0,f0082,f6004,f0110,2f0000,12*0,f0082,f6004
  //   ,f0110,2f0000,12*0,f0082,f6004,f0110,2f0000,12*0,f0082,f6004,f0110
  //   ,2f0000,12*0,f0082,f6004,f0110,2f0000,12*0,f0082,f6004,f0110,2f0000
  //   ,12*0,f0082,f6004,f0110,2f0000,12*0,f0082,f6004,f0110,2f0000,12*0
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  //   32位冯·诺依曼结构微程序控制计算机
  //   contents of ROM (hex, n*v repeats v):
  //   915,8f5a371c,90014,1000000,915,a63f778e,90014,1000001,915,7349bc73
  //   ,90014,1000002,915,13131313,90014,1000003,915,13131313,90014,1000004
  //   ,a15,1000000,b15,1000004,30,1a,a011,a0a22,a111,1002f,32,27,30
  //   ,22,ab02f,33,2e,30,1a,a012,a0a23,1a012,a0a22,c0c22,30,22,cd02f
  //   ,33,37,a15,1000000,c15,0,30,1a,f0
  //   指令集
  //   0x00–0x0F：NOP 和测试草稿区
  //   操作码	助记符	格式	功能
  //   0x00	NOP	R	空操作
  //   0x01–0x0F	(测试草稿)	–	保留用于测试新指令，当前执行 NOP
  //   0x10–0x1F：寄存器和内存控制
  //   操作码	助记符	格式	功能
  //   0x10	MOV	R	Rw ← Ra
  //   0x11	ILD	R	Rw ← M[Rb]（Rb 的内容作为地址读内存）
  //   0x12	IST	R	M[Rb] ← Ra（Rb 的内容作为地址写内存）
  //   0x13	LDR	双字	Rw ← M[addr]（addr 为紧接着的 32 位地址）
  //   0x14	STR	双字	M[addr] ← Ra（addr 为紧接着的 32 位地址）
  //   0x15	LDI	双字	Rw ← imm32（第二字为 32 位立即数）
  //   0x16–0x1F	(保留)	–	可扩展更多访存模式
  //   0x20–0x2F：逻辑运算区
  //   操作码	助记符	格式	功能	ALUMODE
  //   0x20	ADD	R	Rw ← Ra + Rb，更新 C, Z	0000
  //   0x21	SUB	R	Rw ← Ra - Rb，更新 C, Z	0001
  //   0x22	INC	R	Rw ← Ra + 1，不更新标志	1100
  //   0x23	DEC	R	Rw ← Ra - 1，不更新标志	1101
  //   0x24	MUL	R	Rw ← Ra * Rb（低 32 位），更新 C, Z	0010
  //   0x25	DIV	R	Rw ← Ra / Rb（商），更新 C, Z	0011
  //   0x26	REM	R	Rw ← Ra % Rb（余数），更新 Z	1110
  //   0x27	SFT	R	Rw ← Ra 移位（移位量 Rb 低 5 位），更新 C, Z	0100
  //   0x28	AND	R	Rw ← Ra & Rb，更新 Z	0101
  //   0x29	NAND	R	Rw ← ~(Ra & Rb)，更新 Z	0110
  //   0x2A	OR	R	Rw ← Ra | Rb，更新 Z	0111
  //   0x2B	NOR	R	Rw ← ~(Ra | Rb)，更新 Z	1000
  //   0x2C	XOR	R	Rw ← Ra ^ Rb，更新 Z	1001
  //   0x2D	XNOR	R	Rw ← ~(Ra ^ Rb)，更新 Z	1010
  //   0x2E	NOT	R	Rw ← ~Ra，更新 Z	1011
  //   0x2F	CMP	R	Ra - Rb，只更新 C, Z，不写回	0001
  //   0x30–0x3F：程序控制区
  //   操作码	助记符	格式	功能
  //   0x30	JMP	双字	PC ← addr（无条件跳转）
  //   0x31	JPR	R	PC ← Ra（间接跳转）
  //   0x32	JC	双字	若 C=1 则 PC ← addr
  //   0x33	JZ	双字	若 Z=1 则 PC ← addr
  //   0x34	JNC	双字	若 C=0 则 PC ← addr
  //   0x35	JNZ	双字	若 Z=0 则 PC ← addr
  //   0x36	CALL	双字	M[Ra] ← PC，Ra ← Ra + 1，PC ← addr
  //   0x37	RET	R	Ra ← Ra - 1，PC ← M[Ra]
  //   0x38–0x3F	(保留)	–	可扩展条件调用等
  //   0xF0–0xFF：运行管理区
  //   操作码	助记符	格式	功能
  //   0xF0	HALT	R	停机（需外部停时钟）
  //   0xF1–0xFF	(保留)	–	可扩展中断、电源管理等
endmodule
